# Fritzing sketch distance measure (saved by Fritzing 0.9.3b)
breadboards: 1

parts:
  hc-sr1 = hc-sr04
  LED1 = smd LED [color="Red (633nm)" package="0603 [SMD]"]
  LED2 = smd LED [color="Red (633nm)" package="0603 [SMD]"]
  LED3 = smd LED [color="Red (633nm)" package="0603 [SMD]"]
  LED4 = smd LED [color="Red (633nm)" package="0603 [SMD]"]
  LED5 = smd LED [color="Red (633nm)" package="0603 [SMD]"]
  LED6 = smd LED [color="Red (633nm)" package="0603 [SMD]"]
  LED7 = smd LED [color="Red (633nm)" package="0603 [SMD]"]
  Part1 = Arduino Uno (Rev3)
  J1 = Piezo Speaker

nets:
  VCC: hc-sr1.VCC, Part1.5V
  N1: hc-sr1.Trig, Part1.D11_PWM/MOSI
  N2: hc-sr1.Echo, Part1.D12/MISO
  GND: hc-sr1.GND, LED1.cathode, LED2.cathode, LED3.cathode, LED4.cathode, LED5.cathode, LED6.cathode, LED7.cathode, Part1.GND
  N3: Part1.D9_PWM, J1.pin2

// code stored in the sketch: distance measure.ino
  
const int trig = 11; 
const int echo = 12; 
  
const int LED1 = 2; 
const int LED2 = 3; 
const int LED3 = 4; 
const int LED4 = 5; 
const int LED5 = 6; 
const int LED6 = 7; 
const int LED7 = 8; 
const buzzer = 9; 
  
int duration = 0; 
int distance = 0; 
  
void setup() 
{ 
  pinMode(trig , OUTPUT); 
  pinMode(echo , INPUT); 
  
  pinMode(LED1 , OUTPUT); 
  pinMode(LED2 , OUTPUT); 
  pinMode(LED3 , OUTPUT); 
  pinMode(LED4 , OUTPUT); 
  pinMode(LED5 , OUTPUT); 
  pinMode(LED6 , OUTPUT); 
  pinMode(LED7 , OUTPUT); 
pinMODE(buzzer , OUTPUT); 
  
  Serial.begin(9600); 
  
} 
  
void loop() 
{ 
  digitalWrite(trig , HIGH); 
  delayMicroseconds(1000); 
  digitalWrite(trig , LOW); 
  
  
  duration = pulseIn(echo , HIGH); 
  distance = (duration/2) / 28.5 ; 
  Serial.println(distance);  
if ( distance <= 5 ) 
  { 
    digitalWrite(buzzer, HIGH); 
  } 
  else 
  { 
    digitalWrite(buzzer, LOW); 
  } 
  if ( distance <= 5 ) 
  { 
    digitalWrite(LED1, HIGH); 
  } 
  else 
  { 
    digitalWrite(LED1, LOW); 
  } 
  if ( distance <= 7 ) 
  { 
    digitalWrite(LED2, HIGH); 
  } 
  else 
  { 
    digitalWrite(LED2, LOW); 
  } 
  if ( distance <= 10 ) 
  { 
    digitalWrite(LED3, HIGH); 
  } 
  else 
  { 
    digitalWrite(LED3, LOW); 
  } 
  if ( distance <= 15 ) 
  { 
    digitalWrite(LED4, HIGH); 
  } 
  else 
  { 
    digitalWrite(LED4, LOW); 
  } 
  if ( distance <= 17 ) 
  { 
    digitalWrite(LED5, HIGH); 
  } 
  else 
  { 
    digitalWrite(LED5, LOW); 
  } 
  if ( distance <= 20 ) 
  { 
    digitalWrite(LED6, HIGH); 
  } 
  else 
  { 
    digitalWrite(LED6, LOW); 
  } 
  if ( distance <= 25 ) 
  { 
    digitalWrite(LED7, HIGH); 
  } 
  else 
  { 
    digitalWrite(LED7, LOW); 
  } 
}
